// Logisim project Binary_counter.circ as structural Verilog: 1 circuit, main circuit main
module main (
  input  in_1,
  input  in_2
);

  wire _1_out, _2_out, _3_out, _4_out, _5_out, clock_1_out, j_k_ff_1_q, j_k_ff_1_qn, j_k_ff_2_q, j_k_ff_2_qn,
       j_k_ff_3_q, j_k_ff_3_qn, j_k_ff_4_q, j_k_ff_4_qn;

  and _2 (_2_out, j_k_ff_3_q, j_k_ff_4_qn);
  and _1 (_1_out, j_k_ff_3_qn, j_k_ff_4_q);
  Clock clock_1 (.out(clock_1_out));
  LED led_1 (.in(j_k_ff_1_q));
  J_K_Flip_Flop j_k_ff_1 (
    .J(_1_out), .clk(clock_1_out), .K(_2_out), .Q(j_k_ff_1_q), .Qn(j_k_ff_1_qn), .preset(in_1), .reset(in_2));  // open: en
  or _3 (_3_out, j_k_ff_1_qn, _2_out);
  LED led_2 (.in(j_k_ff_2_q));
  J_K_Flip_Flop j_k_ff_2 (
    .J(_3_out), .clk(clock_1_out), .K(j_k_ff_4_q), .Q(j_k_ff_2_q), .Qn(j_k_ff_2_qn), .preset(in_1),
    .reset(in_2));  // open: en
  J_K_Flip_Flop j_k_ff_3 (
    .J(j_k_ff_4_qn), .clk(clock_1_out), .K(_4_out), .Q(j_k_ff_3_q), .Qn(j_k_ff_3_qn), .preset(in_2),
    .reset(in_1));  // open: en
  and _4 (_4_out, j_k_ff_1_qn, _5_out);
  LED led_3 (.in(j_k_ff_3_q));
  or _5 (_5_out, j_k_ff_2_qn, j_k_ff_3_qn, j_k_ff_4_qn);
  LED led_4 (.in(j_k_ff_4_q));
  J_K_Flip_Flop j_k_ff_4 (
    .J(j_k_ff_3_qn), .clk(clock_1_out), .K(j_k_ff_1_q), .Q(j_k_ff_4_q), .Qn(j_k_ff_4_qn), .preset(in_2),
    .reset(in_1));  // open: en

  // Notes on the sheet:
  //   A
  //   B
  //   Reset
  //   C
  //   D
endmodule
